// Digital circuit BW8cpu.dig as structural Verilog
module BW8cpu (
  input  VCC,
  input  GND,
  input  crystal,
  input  _555,
  input  step,
  output [15:0] ADDR,
  output nBRK,
  output [7:0] Mem_Bus
);

  wire a_dbus_a, a_dbus_l, a_lhs_a, a_rhs_a, ab_xfer_l, ack_addr_a, addr_a, alu_dbus_a, alu_res, b_dbus_a,
       b_dbus_l, b_lhs_a, b_rhs_a, c_dbus_a, c_dbus_l, c_lhs_a, c_rhs_a, cd_xfer_l, clk, clk_crystal, count,
       d_dbus_a, d_dbus_l, d_lhs_a, d_rhs_a, da_dbus_a, da_dbus_l, dbus_a, dbus_l, dec_sp, dp_dbus_a,
       dp_dbus_l, ext, flags, ir_dbus_l, lsb_dbus_a, mem_dbus_a, mem_dbus_l, msb_dbus_a, nclk, nirq_latched,
       noffset, nreq_latched, nrst, nRST_out, off_dbus_l, opcode, pc_addr_a, pc_inc, pc_xfer_a, pc_xfer_l,
       pch_dbus_l, pcl_dbus_l, reg_pc, rst, sr_dbus_a, sr_dbus_l, th_dbus_a, tl_dbus_a, xfer_a, xfer_l;
  wire [2:0] Break_out, clk_mode, t_state;
  wire [4:0] alu_op;
  wire [7:0] dbus, lhs, reg_a, reg_b, reg_c, reg_d, reg_da, reg_dp, reg_off, rhs;
  wire [14:3] Control_Unit_p19;
  wire [15:0] addr_t;

  ROM #(.AddrBits(16), .isProgramMemory("true"), .Bits(8)) ROM (.A(ADDR), .sel(1'b1), .D(Mem_Bus));
  // Probe on dbus
  // Probe on {lhs, rhs}
  // Probe on reg_a
  // Probe on reg_b
  // Probe on reg_c
  // Probe on reg_d
  // Probe on reg_dp
  // Probe on reg_da
  PowerSupply powersupply_1 (.VDD(VCC), .GND(GND));
  // Probe on addr_t
  // Probe on Mem_Bus
  // Probe on reg_pc
  // Probe on reg_off
  // Probe on alu_res
  // Probe on nreq_latched
  // Probe on nirq_latched
  // Probe on opcode
  // Probe on ext
  Button u_nRST (.out(nRST_out));
  Button #(.activeLow("true")) Run (.out(Break_out[0]));
  Button #(.activeLow("true")) Demo (.out(Break_out[1]));
  Button #(.activeLow("true")) Break (.out(Break_out[2]));
  // Probe on flags
  // control_unit Control_Unit: pin names not known; wires that end beside it: 1'b1, opcode, flags, 1'b1, clk, nrst, dbus_a, dbus_l, alu_op, xfer_a, xfer_l, addr_a, count, dec_sp, nBRK, nclk, noffset, rst, {nreq_latched, nirq_latched, ext, Control_Unit_p19, t_state}
  // instruction_register Instruction_Register: pin names not known; wires that end beside it: dbus, ir_dbus_l, nrst, opcode
  memory_bridge Memory_Bridge (.dbus_assert(mem_dbus_a), .dbus_load(mem_dbus_l), .dbus(dbus), .mbus(Mem_Bus));
  reset_module reset_module_1 (.clk(clk_crystal), .nrst_in(nRST_out), .nrst(nrst));
  // Probe on t_state
  // triple_clock triple_clock_1: pin names not known; wires that end beside it: Break_out, nBRK, {nrst, 2'b11}, crystal, _555, step, clk, clk_crystal, clk_mode
  // Probe on nclk
  // Probe on nBRK
  LED Run_Mode_Active (.in(clk_mode[0]));
  LED Demo_Mode_Active (.in(clk_mode[1]));
  LED Break_Mode_Active (.in(clk_mode[2]));
  // Probe on dec_sp
  LED cpu (.in(clk));
  LED u_crystal (.in(clk_crystal));
  // Probe on count
  // Probe on addr_a
  // Probe on xfer_l
  // bus_controller Bus_Controller: pin names not known; wires that end beside it: dbus_a, xfer_l, addr_a, clk, count, dec_sp, nclk, dbus_l, xfer_a, alu_dbus_a, a_dbus_a, b_dbus_a, c_dbus_a, d_dbus_a, dp_dbus_a, da_dbus_a, th_dbus_a, tl_dbus_a, sr_dbus_a, mem_dbus_a, msb_dbus_a, lsb_dbus_a, a_dbus_l, b_dbus_l, c_dbus_l
  // Probe on xfer_a
  // Probe on alu_op
  // Probe on dbus_l
  // Probe on dbus_a
  alu Arithmetic___Logic_Unit_and_Status_Register (
    .ALU_OP(alu_op), .LOAD_SR_DBUS(sr_dbus_l), .ASSERT_SR_DBUS(sr_dbus_a), .CLK(nclk), .CLR(rst), .LHS(lhs),
    .RHS(rhs), .ASSERT_ALU_DBUS(alu_dbus_a));  // open: FLAGS, DBUS, q
  gpr_pair A_and_B (
    .naddr_assert(1'b1), .nxfer_load(ab_xfer_l), .nhi_dbus_load(a_dbus_l), .nlo_dbus_load(b_dbus_l),
    .nhi_dbus_assert(a_dbus_a), .nlo_dbus_assert(b_dbus_a), .nhi_lhs_assert(a_lhs_a),
    .nlo_lhs_assert(b_lhs_a), .nhi_rhs_assert(a_rhs_a), .nlo_rhs_assert(b_rhs_a), .dbus(dbus),
    .xfer({lhs, rhs}), .nclr(nrst), .reg_hi(reg_a), .reg_lo(reg_b));  // open: addr
  gpr_pair C_and_D (
    .naddr_assert(1'b1), .nxfer_load(cd_xfer_l), .nhi_dbus_load(c_dbus_l), .nlo_dbus_load(d_dbus_l),
    .nhi_dbus_assert(c_dbus_a), .nlo_dbus_assert(d_dbus_a), .nhi_lhs_assert(c_lhs_a),
    .nlo_lhs_assert(d_lhs_a), .nhi_rhs_assert(c_rhs_a), .nlo_rhs_assert(d_rhs_a), .dbus(dbus),
    .xfer({lhs, rhs}), .nclr(nrst), .reg_hi(reg_c), .reg_lo(reg_d));  // open: addr
  gpr_pair DA_and_DP (
    .naddr_assert(1'b1), .nxfer_load(1'b1), .nhi_dbus_load(dp_dbus_l), .nlo_dbus_load(da_dbus_l),
    .nhi_dbus_assert(dp_dbus_a), .nlo_dbus_assert(da_dbus_a), .nhi_lhs_assert(1'b1), .nlo_lhs_assert(1'b1),
    .nhi_rhs_assert(1'b1), .nlo_rhs_assert(1'b1), .dbus(dbus), .xfer({lhs, rhs}), .nclr(nrst),
    .reg_hi(reg_dp), .reg_lo(reg_da));  // open: addr
  // address_register Program_Counter: pin names not known; wires that end beside it: flags, dbus, alu_res, {lhs, rhs}, rst, pc_xfer_l, pc_addr_a, pc_xfer_a, pc_inc, 1'b1, clk, pch_dbus_l, pcl_dbus_l, dbus, addr_t, reg_pc
  address_offset Address_Bridge (
    .nclk(off_dbus_l), .dbus(dbus), .addr_in(addr_t), .noffset_en(1'b1), .carry_en(1'b0),
    .naddr_xfer_assert(1'b1), .nassert_addr(ack_addr_a), .nclr(nrst), .addr_out(ADDR), .xfer({lhs, rhs}),
    .q(reg_off));

  // Other names for the same wires on the sheet: addr_out[15:0] = ADDR; clk_cpu = clk; mbus[7:0] = Mem_Bus;
  //   rst_clk_mode[2] = nrst; xfer[15:0] = {lhs, rhs}

  // Notes on the sheet:
  //   VCC: default 1
  //   crystal: Hz: 5
  //   ROM loads test.bin
  //   External Pinout
  //   Buses & Constants
  //   Registers
endmodule
